// Logisim project DSDL5.circ as structural Verilog: 1 circuit, main circuit main
module main (
  input  Y0,
  input  Y1,
  input  Y2,
  input  Y3,
  input  X3,
  input  X2,
  input  X1,
  input  X0,
  input  C0,
  output C4,
  output S3,
  output S2,
  output C3,
  output S1,
  output C2,
  output S0,
  output C1
);

  wire G0_out, G1_out, G2_out, G3_out, P0_out, P0C0_out, P0P1P2C0_out, P1_out, P1G0_out, P1P0C0_out, P2_out,
       P2G1_out, P2P1G0_out, P2P3G1_out, P3_out, P3G2_out, P3P2P1G0_out, P3P2P1P0C0_out;

  xor P3 (P3_out, Y3, X3);
  and G3 (G3_out, Y3, X3);
  xor P2 (P2_out, Y2, X2);
  and G2 (G2_out, Y2, X2);
  and G1 (G1_out, Y1, X1);
  and G0 (G0_out, Y0, X0);
  xor P1 (P1_out, Y1, X1);
  xor P0 (P0_out, Y0, X0);
  and P3G2 (P3G2_out, P3_out, G2_out);
  and P2G1 (P2G1_out, P2_out, G1_out);
  and P2P3G1 (P2P3G1_out, P3_out, P2_out, G1_out);
  and P1G0 (P1G0_out, P1_out, G0_out);
  and P2P1G0 (P2P1G0_out, P2_out, P1_out, G0_out);
  and P3P2P1G0 (P3P2P1G0_out, P3_out, P2_out, P1_out, G0_out);
  and P0P1P2C0 (P0P1P2C0_out, P2_out, P1_out, P0_out, C0);
  and P1P0C0 (P1P0C0_out, P1_out, C0, P0_out);
  and P0C0 (P0C0_out, P0_out, C0);
  and P3P2P1P0C0 (P3P2P1P0C0_out, P3_out, P0P1P2C0_out);
  or or_1 (C1, P0C0_out, G0_out);
  or or_2 (C4, P3P2P1P0C0_out, P3P2P1G0_out, P2P3G1_out, P3G2_out, G3_out);
  or or_3 (C3, P2G1_out, P2P1G0_out, P0P1P2C0_out, G2_out);
  or or_4 (C2, P1G0_out, P1P0C0_out, G1_out);
  xor xor_1 (S3, P3_out, C3);
  xor xor_2 (S2, P3_out, C2);
  xor xor_3 (S1, P2_out, C1);
  xor xor_4 (S0, P1_out, C0);
endmodule
